// Logisim project aiAlu.circ as structural Verilog
module and8bit (
  input  [7:0] in_1,
  input  [7:0] in_2,
  output [7:0] out_3
);

  assign out_3 = in_1 & in_2;  // AND_Gate and_1, 8 bits wide
endmodule

module or8bit (
  input  [7:0] in_1,
  input  [7:0] in_2,
  output [7:0] out_3
);

  assign out_3 = in_1 | in_2;  // OR_Gate or_1, 8 bits wide
endmodule

module xor8bit (
  input  [7:0] in_1,
  input  [7:0] in_2,
  output [7:0] out_3
);

  wire [7:0] or_1_out;

  assign out_3 = ~or_1_out;  // NOT_Gate not_1, 8 bits wide
  assign or_1_out = in_1 | in_2;  // OR_Gate or_1, 8 bits wide
endmodule

module halfAdder (
  input  a,
  input  b,
  output S,
  output C
);

  and and_1 (C, a, b);
  xor xor_1 (S, a, b);
endmodule
